# Fritzing sketch mini4lg (saved by Fritzing 0.9.3b)
breadboards: 2

parts:
  ESP1 = ESP32-DevkitC
  VCC1 = Battery
  U1 = TA7291P [package=HSIP10-P-2.54(THT)]
  M1 = DC Motor
  R1 = Resistor [tolerance=±5% resistance=10k package=THT]

nets:
  GND: ESP1.GND, VCC1.-, U1.GND
  N1: ESP1.IO17, U1.IN1
  N2: ESP1.IO16, U1.IN2
  5V: ESP1.5V, U1.Vcc
  N3: VCC1.+, U1.Vs, R1.Pin_1
  N4: U1.OUT1, M1.pin_2
  N5: U1.Vref, R1.Pin_0
  N6: U1.OUT2, M1.pin_1

custom parts:
  TA7291P: The IC are Full-Bridge Driver. 4 modes available (CW / CCW / STOP / BRAKE) and PWM control. Output current:1.0 A (AVE.) 2.0 A (PEAK)
